# Fritzing sketch p1_rgb_led (saved by Fritzing 0.9.9b)
breadboards: 1

parts:
  Part1 = Arduino Uno (Rev3) - ICSP
  R1 = Resistor [tolerance=±5% resistance=1000 package=THT]
  R2 = Resistor [tolerance=±5% resistance=1000 power=0.25 package=THT]
  R3 = Resistor [tolerance=±5% resistance=1000 power=0.25 package=THT]
  S1 = Momentary Switch [package=ksa_sealed_tac_switch]
  R4 = Resistor [tolerance=±5% resistance=10k power=0.25 package=THT]
  LED1 = RGB LED (com. cathode, rgb) [package="5 mm [THT]"]

nets:
  N1: Part1.D10_PWM/SS, R3.Pin_1
  N2: Part1.D11_PWM/MOSI, R2.Pin_1
  N3: Part1.D12/MISO, R1.Pin_1
  N4: Part1.D2, S1.4
  N5: Part1.GND, R4.Pin_1, LED1.common_cathode
  N6: R1.Pin_0, LED1.red_anode
  N7: R2.Pin_0, LED1.blue_anode
  N8: R3.Pin_0, LED1.green_anode
  N9: S1.2, R4.Pin_0

notes:
  Pinout:
  DIO12 -> Red
  DIO11 -> Green
  DIO10 -> Blue
  DIO2 -> Button
