# Fritzing sketch p2_digital_inputs (saved by Fritzing 0.9.9b)
breadboards: 1

parts:
  S1 = Pushbutton [package="[SMD]"]
  S2 = Momentary Switch [package=ksa_sealed_tac_switch]
  Part1 = Arduino Mega 2560 (Rev3)
  S3 = Momentary Switch [package=ksa_sealed_tac_switch]
  LED1 = smd LED [color="Red (633nm)" current=0.030 package="0805 [SMD]"]
  LED2 = smd LED [color="Red (633nm)" current=0.030 package="0805 [SMD]"]
  LED3 = smd LED [color="Red (633nm)" current=0.030 package="0805 [SMD]"]
  R1 = Resistor [tolerance=±5% resistance=1k power=0.25 package=THT]
  R2 = Resistor [tolerance=±5% resistance=1k power=0.25 package=THT]
  R3 = Resistor [tolerance=±5% resistance=1k power=0.25 package=THT]
  R4 = Resistor [tolerance=±5% resistance=10k power=0.25 package=THT]
  R5 = Resistor [tolerance=±5% resistance=10k power=0.25 package=THT]
  R6 = Resistor [tolerance=±5% resistance=10k power=0.25 package=THT]
  C1 = Capacitor [package=cap-pth-small2]

nets:
  N1: S1.Pin_1, S1.Pin_2, R5.Pin_0
  N2: S1.Pin_3, S1.Pin_4, Part1.D2_PWM
  N3: S2.2, R4.Pin_0
  N4: S2.4, Part1.D3_PWM
  N5: Part1.D18/TX1, R6.Pin_0, C1.2
  N6: Part1.D12_PWM, R1.Pin_1
  N7: Part1.D11_PWM, R2.Pin_1
  N8: Part1.D10_PWM, R3.Pin_1
  N9: Part1.GND, S3.2, LED1.cathode, LED2.cathode, LED3.cathode, R4.Pin_1, R5.Pin_1, C1.1
  N10: S3.4, R6.Pin_1
  N11: LED1.anode, R1.Pin_0
  N12: LED2.anode, R2.Pin_0
  N13: LED3.anode, R3.Pin_0

notes:
  Unregulated Input
  Input: 3
  Output: 12
  SW-regulated Input
  Input: 2
  Output: 11
  HW-regulated Input
  Input: 18
  Output: 10
  RC Filter
  R = 10k
  C = 100 nF
  Fc = ~157 Hz
