# Fritzing sketch p3_7seg_counter_grad (saved by Fritzing 0.9.9b)
breadboards: 1

parts:
  Part1 = Arduino Mega 2560 (Rev3)
  LED1 = 7-SEGMENT-4DIGIT-YOUNGSUN [package=7-segment-4digit-youngsun]
  U1 = 74HC595 [package="DIP16 [THT]"]
  R1 = Resistor [tolerance=±5% resistance=220 package="0603 [SMD]"]
  R2 = Resistor [tolerance=±5% resistance=220 package="0603 [SMD]"]
  R3 = Resistor [tolerance=±5% resistance=220 package="0603 [SMD]"]
  R4 = Resistor [tolerance=±5% resistance=220 package="0603 [SMD]"]
  S1 = Pushbutton [package="[THT]"]
  C1 = Capacitor [package=cap-pth-small2]
  R5 = Resistor [tolerance=±5% resistance=10k package="0603 [SMD]"]
  J1 = Piezo Speaker
  Q1 = TRANSISTOR_NPN [package=to-92-ammo]
  R6 = Resistor [tolerance=±5% resistance=1k package="0603 [SMD]"]
  R7 = Resistor [tolerance=±5% resistance=10k package="0603 [SMD]"]
  S2 = Pushbutton [package="[THT]"]
  C2 = Capacitor [package=cap-pth-small2]
  S3 = Pushbutton [package="[THT]"]
  R8 = Resistor [tolerance=±5% resistance=10k package="0603 [SMD]"]
  S4 = Pushbutton [package="[THT]"]
  S5 = Pushbutton [package="[THT]"]
  R9 = Resistor [tolerance=±5% resistance=10k package="0603 [SMD]"]
  R10 = Resistor [tolerance=±5% resistance=10k package="0603 [SMD]"]

nets:
  N1: Part1.D14/TX3, R6.Pin_1
  N2: Part1.D10_PWM, U1.SH_CP
  N3: Part1.D9_PWM, U1.ST_CP
  N4: Part1.D8_PWM, U1.DS
  5V: Part1.5V, U1.MR, U1.VCC
  GND: Part1.GND, U1.GND, U1.OE, S1.Pin_1, S1.Pin_2, C1.1, Q1.E, S2.Pin_1, S2.Pin_2, C2.1, R8.Pin_1, R9.Pin_1, R10.Pin_1
  N5: Part1.D2_PWM, R7.Pin_0, C2.2
  N6: Part1.D3_PWM, C1.2, R5.Pin_0
  N7: Part1.D4_PWM, S5.Pin_3, S5.Pin_4
  N8: Part1.D5_PWM, S4.Pin_3, S4.Pin_4
  N9: Part1.D6_PWM, S3.Pin_3, S3.Pin_4
  N10: Part1.D22, R1.Pin_1
  N11: Part1.D23, R2.Pin_1
  N12: Part1.D24, R3.Pin_1
  N13: Part1.D25, R4.Pin_1
  N14: LED1.DIG2, U1.Q4
  N15: LED1.D, U1.Q3
  N16: LED1.COL-A, U1.Q7
  N17: LED1.E, U1.Q2
  N18: LED1.DIG3, U1.Q6
  N19: LED1.DP, R1.Pin_0
  N20: LED1.APOS-A, U1.Q1
  N21: LED1.F, R2.Pin_0
  N22: LED1.COL-C, R3.Pin_0
  N23: LED1.C, U1.Q5
  N24: LED1.A, U1.Q0
  N25: LED1.G, R4.Pin_0
  N26: S1.Pin_3, S1.Pin_4, R5.Pin_1
  N27: J1.pin1, Q1.C
  N28: Q1.B, R6.Pin_0
  N29: R7.Pin_1, S2.Pin_3, S2.Pin_4
  N30: S3.Pin_1, S3.Pin_2, R8.Pin_0
  N31: S4.Pin_1, S4.Pin_2, R9.Pin_0
  N32: S5.Pin_1, S5.Pin_2, R10.Pin_0

notes:
  Digit Controls
  D1 (Blue) - 22
  D2 (Purp) - 23
  D3 (Pink) - 24
  D4 (Cyan) - 25
  RC Filter
  R = 10k
  C = 100 nF
  Fc = ~157 Hz
  74HC595 Signals
  Data (Blue) - 8
  Latch (Green) - 9
  Clock (Yellow) - 10
  Active buzzer
  NPN transistor (S8050)
  1k resistor
