# Fritzing sketch p3_7seg_counter_ugrad (saved by Fritzing 0.9.10b)
breadboards: 1

parts:
  Part1 = Arduino Mega 2560 (Rev3)
  LED1 = 7-SEGMENT-4DIGIT-YOUNGSUN [package=7-segment-4digit-youngsun]
  U1 = 74HC595 [package="DIP16 [THT]"]
  R1 = Resistor [tolerance=±5% resistance=220 package="0603 [SMD]"]
  R2 = Resistor [tolerance=±5% resistance=220 package="0603 [SMD]"]
  R3 = Resistor [tolerance=±5% resistance=220 package="0603 [SMD]"]
  R4 = Resistor [tolerance=±5% resistance=220 package="0603 [SMD]"]
  S1 = Pushbutton [package="[THT]"]
  C1 = Capacitor [package=cap-pth-small2]
  R5 = Resistor [tolerance=±5% resistance=10k package="0603 [SMD]"]
  J1 = Piezo Speaker
  R6 = Resistor [tolerance=±5% resistance=1k package="0603 [SMD]"]
  Q1 = TRANSISTOR_NPN_2 [package=to-92]
  Q1_2 = TRANSISTOR_NPN [package=to-92-ammo]

nets:
  N1: Part1.D14/TX3, R6.Pin_1
  N2: Part1.D10_PWM, U1.SH_CP
  N3: Part1.D9_PWM, U1.ST_CP
  N4: Part1.D8_PWM, U1.DS
  5V: Part1.5V, U1.MR, U1.VCC
  GND: Part1.GND, U1.GND, U1.OE, S1.Pin_1, S1.Pin_2, C1.1, Q1.E, Q1_2.E
  N5: Part1.D2_PWM, C1.2, R5.Pin_0
  N6: Part1.D22, R1.Pin_1
  N7: Part1.D23, R2.Pin_1
  N8: Part1.D24, R3.Pin_1
  N9: Part1.D25, R4.Pin_1
  N10: LED1.DIG2, U1.Q4
  N11: LED1.D, U1.Q3
  N12: LED1.COL-A, U1.Q7
  N13: LED1.E, U1.Q2
  N14: LED1.DIG3, U1.Q6
  N15: LED1.DP, R1.Pin_0
  N16: LED1.APOS-A, U1.Q1
  N17: LED1.F, R2.Pin_0
  N18: LED1.COL-C, R3.Pin_0
  N19: LED1.C, U1.Q5
  N20: LED1.A, U1.Q0
  N21: LED1.G, R4.Pin_0
  N22: S1.Pin_3, S1.Pin_4, R5.Pin_1
  N23: J1.pin1, Q1.C, Q1_2.C
  N24: R6.Pin_0, Q1.B, Q1_2.B

notes:
  Digit Controls
  D1 (Blue) - 22
  D2 (Purp) - 23
  D3 (Pink) - 24
  D4 (Cyan) - 25
  RC Filter
  R = 10k
  C = 100 nF
  Fc = ~157 Hz
  74HC595 Signals
  Data (Blue) - 8
  Latch (Green) - 9
  Clock (Yellow) - 10
  Active buzzer
  NPN transistor (S8050)
  1k resistor
