# Fritzing sketch supplement_rpi_icsp (saved by Fritzing 0.9.9b)
breadboards: 1

parts:
  Part1 = Adafruit T-Cobbler Plus [part_number="Adafruit #1989 and #2028"]
  Part3 = Arduino Uno (Rev3) - ICSP
  Part4 = Adafruit 4-channel I2C-safe Bi-directional Logic Level Converter [part_number="Adafruit #757"]

nets:
  N1: Part1.+3.3V, Part1.+3.3V_2, Part4.LV
  GND: Part1.GND, Part3.GND, Part4.GND
  N2: Part1.GPIO17, Part4.A1
  N3: Part1.MOSI, Part4.A4
  N4: Part1.MISO, Part4.A3
  N5: Part1.SCLK, Part4.A2
  +5V: Part1.+5V, Part3.5V, Part4.HV
  N6: Part3.ICSP_MISO, Part3.D12/MISO, Part4.B3
  N7: Part3.ICSP_SCK, Part4.B2
  N8: Part3.ICSP_MOSI, Part4.B4
  N9: Part3.RESET, Part4.B1

notes:
  MISO (Blue) | 5V (Red)
  SCK (Yellow) | MOSI (Green)
  RST (White) | GND (Black)

custom parts:
  Adafruit T-Cobbler Plus: The Raspberry Pi has landed on the Maker World like a 40-GPIO pinned, quad-USB ported, credit card sized bomb of DIY joy. And while you can use most of our great Model B accessories by hooking up our downgrade cable, its probably a good time to upgrade your set up and accessorize using all of the 40 pins. That's why we now carry the Assembled Adafruit Pi T-Cobbler Plus - Breakout + Cable for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
  Adafruit 4-channel I2C-safe Bi-directional Logic Level Converter: Because the Arduino (and Basic Stamp) are 5V devices, and most modern sensors, displays, flash cards and modes are 3.3V-only, many makers find that they need to perform level shifting/conversion to protect the 3.3V device from 5V. We do have some other handy level shifters in the shop, from the DIP 74LVC245 to the fancy bi-directional TXB0108. However, neither of these are happy to work with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
