# Fritzing sketch basic_logic_gates_2_sch (saved by Fritzing 0.9.10b)
breadboards: 1

parts:
  Part1 = Arduino Mega 2560 (Rev3)
  S1 = Pushbutton [package="[THT]"]
  S2 = Pushbutton [package="[THT]"]
  S3 = Pushbutton [package="[THT]"]
  S4 = Pushbutton [package="[THT]"]
  LED1 = LED - 5mm [color="Red (633nm)" current=0.030 package="5 mm [THT]"]
  R1 = Resistor [tolerance=±5% resistance=220 package="0402 [SMD]"]

nets:
  N1: Part1.D13_PWM, R1.Pin_0
  N2: Part1.GND, Part1.D2_PWM, Part1.D3_PWM, Part1.D4_PWM, Part1.D5_PWM, S1.Pin_3, S1.Pin_4, S2.Pin_3, S2.Pin_4, S3.Pin_3, S3.Pin_4, S4.Pin_3, S4.Pin_4, LED1.anode
  N3: S1.Pin_1, S1.Pin_2
  N4: S2.Pin_1, S2.Pin_2
  N5: S3.Pin_1, S3.Pin_2
  N6: S4.Pin_1, S4.Pin_2
  N7: LED1.cathode, R1.Pin_1
